// Logisim project s-mips.circ as structural Verilog
module S_MIPS_Board (
  input  DESHABILITAR_DISPATCHER,
  output halt
);

  wire button_1_out, CLK, CS, d_ff_1_q, LCLR, LoadRAM, LoadRAMOn, LW, R_R_W, R_W, ram_dispatcher_1_finished,
       RCS, Reset_out, RST, TTY_EN;
  wire [2:0] KDB;
  wire [3:0] LMask, Mask, ram_1_read_time, ram_1_write_time, RMask;
  wire [6:0] KDB_DATA, TTY_DATA;
  wire [15:0] Addr, LAddr, RAddr;
  wire [31:0] I0, I1, I2, I3, LData, ram_1_data_out_0, ram_1_data_out_1, ram_1_data_out_2, ram_1_data_out_3,
       RI0, RI1, RI2, RI3;

  TTY #(.rows(25), .cols(80)) tty_1 (.data(TTY_DATA), .clk(CLK), .we(TTY_EN), .clr(RST));
  not not_1 (LoadRAMOn, ram_dispatcher_1_finished);
  RAM_Dispatcher ram_dispatcher_1 (
    .WriteTime(ram_1_write_time), .Clock(CLK), .Data(LData), .Address(LAddr), .Mask(LMask),
    .Finished(ram_dispatcher_1_finished), .Write(LW), .CLR(LCLR));
  Keyboard #(.buflen(64)) keyboard_1 (.clk(CLK), .re(KDB[0]), .avail(KDB[2]), .data(KDB_DATA));  // open: clr
  RAM ram_1 (
    .Address(RAddr), .Data_Out_0(ram_1_data_out_0), .Data_Out_1(ram_1_data_out_1),
    .Data_Out_2(ram_1_data_out_2), .Data_Out_3(ram_1_data_out_3), .Data_In_0(RI0), .Data_In_1(RI1),
    .Data_In_2(RI2), .Data_In_3(RI3), .Mask(RMask), .nRead_Write(R_R_W), .Chip_Select(RCS),
    .Read_Time(ram_1_read_time), .Reset(button_1_out), .Write_Time(ram_1_write_time));
  Button button_1 (.out(button_1_out));
  D_Flip_Flop d_ff_1 (.clk(CLK), .D(1'b1), .Q(d_ff_1_q), .reset(Reset_out));  // open: Qn, preset, en
  Button Reset (.out(Reset_out));
  S_MIPS s_mips_1 (
    .Kbd_Enable(KDB[0]), .Address(Addr), .Kbd_Clear(KDB[1]), .Kbd_Available(KDB[2]),
    .Kbd_ASCII_Data(KDB_DATA), .TTY_Enable(TTY_EN), .TTY_ASCII_Data(TTY_DATA), .Reset(RST),
    .RAM_Out_0(ram_1_data_out_0), .Clock(CLK), .RAM_Out_1(ram_1_data_out_1), .Stop(halt),
    .RAM_Out_2(ram_1_data_out_2), .RAM_Out_3(ram_1_data_out_3), .Mask(Mask), .Read_Time(ram_1_read_time),
    .Write_Time(ram_1_write_time), .nRead_Write(R_W), .Chip_Select(CS), .RAM_In_0(I0), .RAM_In_1(I1),
    .RAM_In_2(I2), .RAM_In_3(I3));
  D_Flip_Flop d_ff_2 (.clk(CLK), .D(d_ff_1_q), .Qn(LCLR), .reset(Reset_out));  // open: Q, preset, en
  or or_1 (RST, LCLR, LoadRAM);
  Clock clock_1 (.out(CLK));
  Multiplexer #(.width(32), .enable("false")) multiplexer_1 (.in0(I0), .in1(LData), .out(RI0), .sel(LoadRAM));
  Multiplexer #(.width(32), .enable("false")) multiplexer_2 (.in0(I1), .in1(LData), .out(RI1), .sel(LoadRAM));
  Multiplexer #(.width(32), .enable("false")) multiplexer_3 (.in0(I2), .in1(LData), .out(RI2), .sel(LoadRAM));
  Multiplexer #(.width(32), .enable("false")) multiplexer_4 (.in0(I3), .in1(LData), .out(RI3), .sel(LoadRAM));
  and and_1 (LoadRAM, ~DESHABILITAR_DISPATCHER, LoadRAMOn);  // AND_Gate
  Multiplexer #(.width(16), .enable("false")) multiplexer_5 (.in0(Addr), .in1(LAddr), .out(RAddr), .sel(LoadRAM));
  Multiplexer #(.width(4), .enable("false")) multiplexer_6 (.in0(Mask), .in1(LMask), .out(RMask), .sel(LoadRAM));
  Multiplexer #(.enable("false")) multiplexer_7 (.in0(CS), .in1(LW), .out(RCS), .sel(LoadRAM));
  Multiplexer #(.enable("false")) multiplexer_8 (.in0(R_W), .in1(LW), .out(R_R_W), .sel(LoadRAM));

  // Notes on the sheet:
  //   NO MODIFICAR
  //   Keyboard
endmodule

module RAM (
  input  [15:0] Address,
  input  [31:0] Data_In_0,
  input  [31:0] Data_In_1,
  input  [31:0] Data_In_2,
  input  [31:0] Data_In_3,
  input  [3:0] Mask,
  input  nRead_Write,
  input  Chip_Select,
  input  Reset,
  output [31:0] Data_Out_0,
  output [31:0] Data_Out_1,
  output [31:0] Data_Out_2,
  output [31:0] Data_Out_3,
  output [3:0] Read_Time,
  output [3:0] Write_Time
);

  wire and_2_out, and_3_out, and_4_out, and_5_out, and_6_out, and_7_out, and_8_out, and_9_out, Changed, CLK,
       comparator_2_eq, comparator_3_eq, comparator_4_eq, comparator_5_eq, comparator_6_eq, Count,
       demultiplexer_3_out0, Idle, Idle_q, Load, Load0, Load1, nand_1_out, or_1_out, or_2_out, or_3_out,
       or_4_out, or_5_out, or_6_out, or_7_out, or_8_out, or_9_out, or_10_out, Proc_q, Update_Mem, Zero_Time;
  wire [3:0] counter_1_q, multiplexer_1_out, subtractor_1_out;
  wire [31:0] register_1_q, register_2_q, register_3_q, register_4_q, register_5_q;

  // Probe on 4'b0011
  // Probe on 4'b0010
  Multiplexer #(.width(4), .enable("false")) multiplexer_1 (
    .in0(4'b0011), .in1(4'b0010), .out(multiplexer_1_out), .sel(nRead_Write));
  or or_1 (or_1_out, Idle, Update_Mem);
  or or_2 (or_2_out, ~Chip_Select, Reset);  // OR_Gate
  Subtractor #(.width(4)) subtractor_1 (.a(multiplexer_1_out), .b(4'b0010), .out(subtractor_1_out));  // open: bin, bout
  Demultiplexer #(.enable("false")) demultiplexer_1 (.out0(Idle), .out1(Load0), .in(Idle_q), .sel(Changed));
  D_Flip_Flop u_Idle (.clk(CLK), .D(or_1_out), .Q(Idle_q), .preset(or_2_out));  // open: Qn, en, reset
  // Probe on counter_1_q
  Counter #(.width(4), .max('hf)) counter_1 (
    .load(Load), .D(subtractor_1_out), .count(Count), .Q(counter_1_q), .clk(CLK), .clr(or_3_out));  // open: carry
  or or_3 (or_3_out, ~Chip_Select, Reset);  // OR_Gate
  Comparator #(.width(4), .mode("unsigned")) comparator_1 (
    .a(4'b0000), .b(counter_1_q), .eq(Zero_Time));  // open: gt, lt
  or or_4 (or_4_out, Count, Load0, Load1);
  Register #(.width(32)) register_1 (.D(Data_In_0), .en(Chip_Select), .Q(register_1_q), .clk(CLK), .clr(or_5_out));
  or or_5 (or_5_out, ~Chip_Select, Reset);  // OR_Gate
  Register #(.width(32)) register_2 (.D(Data_In_1), .en(Chip_Select), .Q(register_2_q), .clk(CLK), .clr(or_6_out));
  or or_6 (or_6_out, ~Chip_Select, Reset);  // OR_Gate
  Register #(.width(32)) register_3 (.D(Data_In_2), .en(Chip_Select), .Q(register_3_q), .clk(CLK), .clr(or_7_out));
  or or_7 (or_7_out, ~Chip_Select, Reset);  // OR_Gate
  Register #(.width(32)) register_4 (.D(Data_In_3), .en(Chip_Select), .Q(register_4_q), .clk(CLK), .clr(or_8_out));
  or or_8 (or_8_out, ~Chip_Select, Reset);  // OR_Gate
  Register #(.width(32)) register_5 (
    .D({{11{1'b1}}, nRead_Write, Mask, Address}), .en(Chip_Select), .Q(register_5_q), .clk(CLK),
    .clr(or_9_out));
  or or_9 (or_9_out, ~Chip_Select, Reset);  // OR_Gate
  D_Flip_Flop Proc (.clk(CLK), .D(or_4_out), .Q(Proc_q), .reset(or_10_out));  // open: Qn, preset, en
  or or_10 (or_10_out, ~Chip_Select, Reset);  // OR_Gate
  Demultiplexer #(.enable("false")) demultiplexer_2 (
    .out0(Count), .out1(Update_Mem), .in(demultiplexer_3_out0), .sel(Zero_Time));
  Demultiplexer #(.enable("false")) demultiplexer_3 (
    .out0(demultiplexer_3_out0), .out1(Load1), .in(Proc_q), .sel(Changed));
  Clock clock_1 (.out(CLK));
  Comparator #(.width(32)) comparator_2 (.a(register_1_q), .b(Data_In_0), .eq(comparator_2_eq));  // open: gt, lt
  Comparator #(.width(32)) comparator_3 (.a(register_2_q), .b(Data_In_1), .eq(comparator_3_eq));  // open: gt, lt
  Comparator #(.width(32)) comparator_4 (.a(register_3_q), .b(Data_In_2), .eq(comparator_4_eq));  // open: gt, lt
  Comparator #(.width(32)) comparator_5 (.a(register_4_q), .b(Data_In_3), .eq(comparator_5_eq));  // open: gt, lt
  Comparator #(.width(32)) comparator_6 (
    .a(register_5_q), .b({{11{1'b1}}, nRead_Write, Mask, Address}), .eq(comparator_6_eq));  // open: gt, lt
  nand nand_1 (nand_1_out, comparator_6_eq, comparator_2_eq, comparator_3_eq, comparator_4_eq, comparator_5_eq);
  and and_1 (Changed, nand_1_out, Chip_Select);
  or or_11 (Load, Count, Load1, Load0);
  and and_2 (and_2_out, Mask[0], Update_Mem, nRead_Write);
  and and_3 (and_3_out, Mask[1], Update_Mem, nRead_Write);
  and and_4 (and_4_out, Mask[2], Update_Mem, nRead_Write);
  and and_5 (and_5_out, Mask[3], Update_Mem, nRead_Write);
  RAM_part #(.addrWidth(16), .dataWidth(32), .bus("separate")) ram_1 (
    .addr(Address), .din(Data_In_0), .data(Data_Out_0), .str(and_2_out), .sel(Chip_Select), .clk(CLK),
    .ld(and_6_out), .clr(Reset));
  and and_6 (and_6_out, ~nRead_Write, Idle);  // AND_Gate
  RAM_part #(.addrWidth(16), .dataWidth(32), .bus("separate")) ram_2 (
    .addr(Address), .din(Data_In_1), .data(Data_Out_1), .str(and_3_out), .sel(Chip_Select), .clk(CLK),
    .ld(and_7_out), .clr(Reset));
  and and_7 (and_7_out, ~nRead_Write, Idle);  // AND_Gate
  RAM_part #(.addrWidth(16), .dataWidth(32), .bus("separate")) ram_3 (
    .addr(Address), .din(Data_In_2), .data(Data_Out_2), .str(and_4_out), .sel(Chip_Select), .clk(CLK),
    .ld(and_8_out), .clr(Reset));
  and and_8 (and_8_out, ~nRead_Write, Idle);  // AND_Gate
  RAM_part #(.addrWidth(16), .dataWidth(32), .bus("separate")) ram_4 (
    .addr(Address), .din(Data_In_3), .data(Data_Out_3), .str(and_5_out), .sel(Chip_Select), .clk(CLK),
    .ld(and_9_out), .clr(Reset));
  and and_9 (and_9_out, ~nRead_Write, Idle);  // AND_Gate

  assign Read_Time = 4'b0011;
  assign Write_Time = 4'b0010;

  // Other names for the same wires on the sheet: M0 = Mask[0]; M1 = Mask[1]; M2 = Mask[2]; M3 = Mask[3];
  //   RW = nRead_Write; CLR = Reset; CS = Chip_Select; Load2 = Count

  // Notes on the sheet:
  //   NO MODIFICAR
  //   excepto quizás los valores RT y WT
  //   BANK0
  //   BANK1
  //   BANK2
  //   BANK3
endmodule

module S_MIPS (
  input  Kbd_Available,
  input  [6:0] Kbd_ASCII_Data,
  input  [31:0] RAM_Out_0,
  input  [31:0] RAM_Out_1,
  input  Reset,
  input  [31:0] RAM_Out_2,
  input  Clock,
  input  [31:0] RAM_Out_3,
  input  [3:0] Read_Time,
  input  [3:0] Write_Time,
  output Kbd_Enable,
  output [15:0] Address,
  output Kbd_Clear,
  output TTY_Enable,
  output [31:0] RAM_In_0,
  output [6:0] TTY_ASCII_Data,
  output [31:0] RAM_In_1,
  output Stop,
  output [31:0] RAM_In_2,
  output [31:0] RAM_In_3,
  output [3:0] Mask,
  output nRead_Write,
  output Chip_Select
);

  wire IM, LH, PC, R_Rtart, R_Write, RAM_Ready, RF, S_A, S_DA, S_DO, SP;
  wire [1:0] Bank, S_ADR, S_B, S_BC;
  wire [2:0] S_ALU, S_DI, S_Flag;
  wire [5:0] FuncCode, OpCode;
  wire [31:0] Address_t, convert_1_output, Data_Out, RAM_Data;

  Control_Unit_2 control_unit_1 (
    .in_1(OpCode), .in_2(FuncCode), .in_3(Clock), .in_4(Reset), .in_5(RAM_Ready), .Output(IM), .out_7(S_ALU),
    .out_8(S_DI), .out_11(S_ADR), .out_13(S_A), .out_15(S_B), .out_20(S_BC), .out_16(S_DO), .out_18(S_Flag),
    .out_21(S_DA), .out_9(LH), .out_12(R_Write), .out_14(TTY_Enable), .out_19(R_Rtart), .out_22(Kbd_Enable),
    .out_10(RF), .out_17(PC), .out_23(SP), .out_24(Stop));
  MemoryManager memorymanager_1 (
    .Addres_In(Address_t), .Ram_out_0(RAM_Out_0), .Ram_out_1(RAM_Out_1), .Ram_out_2(RAM_Out_2),
    .Ram_out_3(RAM_Out_3), .Read_Time(Read_Time), .Clk(Clock), .Rst(Reset), .Write_Time(Write_Time),
    .Start(R_Rtart), .R_W(R_Write), .From_RAM(RAM_Data), .Mask(Mask), .ADDR(Address), .Bank(Bank),
    .RAMReady(RAM_Ready), .Chip_Select(Chip_Select), .RAM_Write(nRead_Write));
  DataPath datapath_1 (
    .DI(RAM_Data), .in_1(S_DA), .in_3(S_DO), .in_4(S_A), .in_5(Clock), .in_9(IM), .in_11(PC), .in_12(LH),
    .in_14(RF), .in_16(SP), .in_7(Reset), .in_13(S_DI), .in_15(S_ALU), .in_17(S_Flag), .in_6(S_B),
    .in_8(S_BC), .in_10(S_ADR), .Address(Address_t), .Data_Out(Data_Out), .out_24(TTY_ASCII_Data),
    .kbd_data(Kbd_ASCII_Data), .Opcode(OpCode), .Funcode(FuncCode), .avail(Kbd_Available));
  Demultiplexer #(.select(2), .width(32), .enable("false")) demultiplexer_1 (
    .out0(RAM_In_0), .out1(RAM_In_1), .out2(RAM_In_2), .out3(RAM_In_3), .in(convert_1_output), .sel(Bank));
  Convert convert_1 (.Input(Data_Out), .Output(convert_1_output));

  assign Kbd_Clear = Reset;

  // Other names for the same wires on the sheet: CLK = Clock; CS = Chip_Select; KBD_AVAIL = Kbd_Available;
  //   KBD_DATA[6:0] = Kbd_ASCII_Data; RAM_A[15:0] = Address; RAM_MASK[3:0] = Mask; RAM_OUTPUT_0[31:0] = RAM_Out_0;
  //   RAM_OUTPUT_1[31:0] = RAM_Out_1; RAM_OUTPUT_2[31:0] = RAM_Out_2; RAM_OUTPUT_3[31:0] = RAM_Out_3; RST = Reset;
  //   RW = nRead_Write; TTY_DATA[6:0] = TTY_ASCII_Data

  // Notes on the sheet:
  //   RAM ADDRESS
  //   DATA FROM RAM
  //   KEYBOARD
  //   TTY
  //   SEQUENCING
  //   DATA TO RAM
  //   RAM TIMING
  //   RAM CONTROL
  //   DATA WRITE MASK
endmodule

module RAM_Dispatcher (
  input  [3:0] WriteTime,
  input  Clock,
  input  CLR,
  output [31:0] Data,
  output [15:0] Address,
  output [3:0] Mask,
  output Finished,
  output Write
);

  wire demultiplexer_2_out1, demultiplexer_3_out1, End, IDLE_q, IncAddr, Load, or_1_out, or_2_out, While_q,
       WriteEnd;
  wire [3:0] counter_1_q;
  wire [31:0] CurrentAddress_q;

  Counter #(.width(32), .max('hffffffff)) CurrentAddress (
    .count(IncAddr), .Q({CurrentAddress_q[31:18], Address, CurrentAddress_q[1:0]}), .clk(Clock), .clr(CLR));  // open: load, D, carry
  or or_1 (or_1_out, IncAddr, demultiplexer_3_out1, Finished);
  D_Flip_Flop IDLE (.clk(Clock), .D(or_1_out), .Q(IDLE_q), .preset(CLR));  // open: Qn, en, reset
  Demultiplexer #(.enable("false")) demultiplexer_1 (.out0(Load), .out1(Finished), .in(IDLE_q), .sel(End));
  D_Flip_Flop While (.clk(Clock), .D(or_2_out), .Q(While_q), .reset(CLR));  // open: Qn, preset, en
  or or_2 (or_2_out, Write, Load);
  RAM_part #(.addrWidth(18), .dataWidth(32)) ram_1 (
    .addr({Address, CurrentAddress_q[1:0]}), .data(Data), .clk(Clock));  // open: sel, ld, clr
  Demultiplexer #(.enable("false")) demultiplexer_2 (
    .out0(Write), .out1(demultiplexer_2_out1), .in(While_q), .sel(WriteEnd));
  Decoder #(.select(2)) decoder_1 (
    .out0(Mask[0]), .out1(Mask[1]), .out2(Mask[2]), .out3(Mask[3]), .sel(CurrentAddress_q[1:0]));  // open: en
  Demultiplexer #(.enable("false")) demultiplexer_3 (
    .out0(IncAddr), .out1(demultiplexer_3_out1), .in(demultiplexer_2_out1), .sel(End));
  Counter #(.width(4), .max('hf)) counter_1 (
    .load(Load), .D(WriteTime), .count(Write), .Q(counter_1_q), .clk(Clock));  // open: carry, clr
  Comparator #(.width(32)) comparator_1 (.a(Data), .b({32{1'b1}}), .eq(End));  // open: gt, lt
  Comparator #(.width(4)) comparator_2 (.a(4'b0000), .b(counter_1_q), .eq(WriteEnd));  // open: gt, lt

  // Other names for the same wires on the sheet: CLK = Clock; Count = Write; WT[3:0] = WriteTime
endmodule

module ALU_2 (
  input  [31:0] in_1,
  input  [31:0] in_2,
  input  [2:0] S,
  output [31:0] Lo,
  output [31:0] R,
  output [31:0] Hi,
  output Positive,
  output Zero,
  output Negative
);

  wire comparator_1_lt, comparator_2_lt;
  wire [31:0] And, Diff, HiDiv, HiDivu, HiMult, HiMulu, LoDiv, LoDivu, LoMult, LoMulu, Nor, Or, Slt, Sltu,
       Sum, Xor;

  Adder #(.width(32)) adder_1 (.a(in_1), .b(in_2), .out(Sum));  // open: cin, cout
  Subtractor #(.width(32)) subtractor_1 (.a(in_1), .b(in_2), .out(Diff));  // open: bin, bout
  Comparator #(.width(32)) comparator_1 (.a(in_1), .b(in_2), .lt(comparator_1_lt));  // open: gt, eq
  Comparator #(.width(32), .mode("unsigned")) comparator_2 (.a(in_1), .b(in_2), .lt(comparator_2_lt));  // open: gt, eq
  assign Sltu = {{31{1'b0}}, comparator_2_lt};  // Bit_Extender bit_extender_1
  // Probe on in_1
  assign Slt = {{31{1'b0}}, comparator_1_lt};  // Bit_Extender bit_extender_2
  Multiplier #(.width(32)) multiplier_1 (.a(in_1), .b(in_2), .out(LoMulu), .cout(HiMulu));  // open: cin
  Divider_part #(.width(32)) divider_1 (.a(in_1), .b(in_2), .out(LoDivu), .rem(HiDivu));  // open: upper
  // Probe on in_2
  Multipler multipler_1 (.in_1(in_1), .in_2(in_2), .out_3(LoMult), .out_4(HiMult));
  Divider divider_2 (.in_1(in_1), .in_2(in_2), .out_3(LoDiv), .out_4(HiDiv));
  Multiplexer #(.select(2), .width(32), .enable("false")) multiplexer_1 (
    .in0(LoMulu), .in1(LoMult), .in2(LoDiv), .in3(LoDivu), .out(Lo), .sel(S[1:0]));
  Multiplexer #(.select(2), .width(32), .enable("false")) multiplexer_2 (
    .in0(HiMulu), .in1(HiMult), .in2(HiDiv), .in3(HiDivu), .out(Hi), .sel(S[1:0]));
  assign And = in_1 & in_2;  // AND_Gate and_1, 32 bits wide
  assign Or = in_1 | in_2;  // OR_Gate or_1, 32 bits wide
  assign Nor = ~Or;  // NOT_Gate not_1, 32 bits wide
  assign Xor = in_1 ^ in_2;  // XOR_Gate xor_1, 32 bits wide
  Multiplexer #(.select(3), .width(32), .enable("false")) multiplexer_3 (
    .in0(Sum), .in1(Diff), .in2(And), .in3(Or), .in4(Nor), .in5(Xor), .in6(Slt), .in7(Sltu), .out(R), .sel(S));
  Comparator #(.width(32)) comparator_3 (.a(R), .b({32{1'b0}}), .gt(Positive), .eq(Zero), .lt(Negative));

  // Other names for the same wires on the sheet: A[31:0] = in_1; B[31:0] = in_2; LoHi_S[1:0] = S[1:0]

  // Notes on the sheet:
  //   Comparation
  //   Unisgned
  //   Aritmethic Op
  //   ALU
  //   Logic Op
  //   Outputs
endmodule

module Abs (
  input  [31:0] In,
  output [31:0] Out,
  output Sign
);

  wire [31:0] negator_1_out;

  BitSelector #(.width(32)) bitselector_1 (.in(In), .out(Sign), .sel({5{1'b1}}));
  Multiplexer #(.width(32), .enable("false")) multiplexer_1 (.in0(In), .in1(negator_1_out), .out(Out), .sel(Sign));
  Negator #(.width(32)) negator_1 (.in(In), .out(negator_1_out));

  // Notes on the sheet:
  //   Absolute Value and Sign
endmodule

module Multipler (
  input  [31:0] in_1,
  input  [31:0] in_2,
  output [31:0] out_3,
  output [31:0] out_4
);

  wire adder_1_cout, Sign_A, Sign_B, Sing_F;
  wire [31:0] abs_1_out, abs_2_out, High, Low, minus_High, minus_Low, not_1_out, not_2_out;

  Abs abs_1 (.In(in_1), .Out(abs_1_out), .Sign(Sign_A));
  Abs abs_2 (.In(in_2), .Out(abs_2_out), .Sign(Sign_B));
  xor xor_1 (Sing_F, Sign_A, Sign_B);
  Multiplier #(.width(32)) multiplier_1 (.a(abs_1_out), .b(abs_2_out), .out(Low), .cout(High));  // open: cin
  assign not_1_out = ~Low;  // NOT_Gate not_1, 32 bits wide
  Adder #(.width(32)) adder_1 (.a(not_1_out), .b(32'h1), .out(minus_Low), .cout(adder_1_cout));  // open: cin
  assign not_2_out = ~High;  // NOT_Gate not_2, 32 bits wide
  Adder #(.width(32)) adder_2 (.a(not_2_out), .b({32{1'b0}}), .out(minus_High), .cin(adder_1_cout));  // open: cout
  Multiplexer #(.width(32), .enable("false")) multiplexer_1 (.in0(Low), .in1(minus_Low), .out(out_3), .sel(Sing_F));
  Multiplexer #(.width(32), .enable("false")) multiplexer_2 (.in0(High), .in1(minus_High), .out(out_4), .sel(Sing_F));

  // Notes on the sheet:
  //   A
  //   B
  //   FInal Sign
  //   Multipler
  //   Negator
  //   Output
  //   Low
  //   High
endmodule

module Divider (
  input  [31:0] in_1,
  input  [31:0] in_2,
  output [31:0] out_3,
  output [31:0] out_4
);

  wire Sign_A, Sign_B, Sing_F;
  wire [31:0] abs_1_out, abs_2_out, High, Low, minus_High, minus_Low;

  // Probe on in_1
  // Probe on in_2
  Abs abs_1 (.In(in_1), .Out(abs_1_out), .Sign(Sign_A));
  Abs abs_2 (.In(in_2), .Out(abs_2_out), .Sign(Sign_B));
  xor xor_1 (Sing_F, Sign_A, Sign_B);
  Divider_part #(.width(32)) divider_1 (.a(abs_1_out), .b(abs_2_out), .out(Low), .rem(High));  // open: upper
  Negator #(.width(32)) negator_1 (.in(Low), .out(minus_Low));
  Negator #(.width(32)) negator_2 (.in(High), .out(minus_High));
  // Probe on out_3
  Multiplexer #(.width(32), .enable("false")) multiplexer_1 (.in0(Low), .in1(minus_Low), .out(out_3), .sel(Sing_F));
  // Probe on out_4
  Multiplexer #(.width(32), .enable("false")) multiplexer_2 (.in0(High), .in1(minus_High), .out(out_4), .sel(Sign_A));

  // Notes on the sheet:
  //   FInal Sign
  //   Divider
  //   Negator
  //   Output
  //   Low
  //   High
endmodule

module Register_File_2 (
  input  Red_Write,
  input  [4:0] DA,
  input  [31:0] DI,
  input  [4:0] SA,
  input  Clk,
  input  Reset,
  input  [4:0] SB,
  input  Low_High,
  input  [31:0] SP,
  input  SP_RW,
  input  [31:0] Low,
  input  [31:0] High,
  output [31:0] out_13,
  output [31:0] out_14,
  output [31:0] out_15,
  output [31:0] out_16,
  output [31:0] out_17
);

  wire Ld00, Ld01, Ld02, Ld03, Ld04, Ld05, Ld06, Ld07, Ld08, Ld09, Ld10, Ld11, Ld12, Ld13, Ld14, Ld15, Ld16,
       Ld17, Ld18, Ld19, Ld20, Ld21, Ld22, Ld23, Ld24, Ld25, Ld26, Ld27, Ld28, Ld29, Ld30, Ld31, SPW;
  wire [31:0] R01, R02, R03, R04, R05, R06, R07, R08, R09, R10, R11, R12, R13, R14, R15, R16, R17, R18, R19,
       R20, R21, R22, R23, R24, R25, R26, R27, R28, R29, R30;

  Decoder #(.select(5), .disabled(0)) decoder_1 (
    .out0(Ld00), .out1(Ld01), .out2(Ld02), .out3(Ld03), .out4(Ld04), .out5(Ld05), .out6(Ld06), .out7(Ld07),
    .out8(Ld08), .out9(Ld09), .out10(Ld10), .out11(Ld11), .out12(Ld12), .out13(Ld13), .out14(Ld14),
    .out15(Ld15), .out16(Ld16), .out17(Ld17), .out18(Ld18), .out19(Ld19), .out20(Ld20), .out21(Ld21),
    .out22(Ld22), .out23(Ld23), .out24(Ld24), .out25(Ld25), .out26(Ld26), .out27(Ld27), .out28(Ld28),
    .out29(Ld29), .out30(Ld30), .out31(Ld31), .sel(DA), .en(Red_Write));
  or or_1 (SPW, SP_RW, Ld31);
  Register #(.width(32), .trigger("falling")) register_1 (.D(DI), .en(Ld04), .Q(R04), .clk(Clk), .clr(Reset));
  Register #(.width(32), .trigger("falling")) register_2 (.D(DI), .en(Ld08), .Q(R08), .clk(Clk), .clr(Reset));
  Register #(.width(32), .trigger("falling")) register_3 (.D(DI), .en(Ld12), .Q(R12), .clk(Clk), .clr(Reset));
  Register #(.width(32), .trigger("falling")) register_4 (.D(DI), .en(Ld16), .Q(R16), .clk(Clk), .clr(Reset));
  Register #(.width(32), .trigger("falling")) register_5 (.D(DI), .en(Ld20), .Q(R20), .clk(Clk), .clr(Reset));
  Register #(.width(32), .trigger("falling")) register_6 (.D(DI), .en(Ld24), .Q(R24), .clk(Clk), .clr(Reset));
  Register #(.width(32), .trigger("falling")) register_7 (.D(DI), .en(Ld28), .Q(R28), .clk(Clk), .clr(Reset));
  Register #(.width(32), .trigger("falling")) register_8 (.D(DI), .en(Ld29), .Q(R29), .clk(Clk), .clr(Reset));
  Register #(.width(32), .trigger("falling")) RHi (.D(High), .en(Low_High), .Q(out_16), .clk(Clk), .clr(Reset));
  Register #(.width(32), .trigger("falling")) register_9 (.D(DI), .en(Ld01), .Q(R01), .clk(Clk), .clr(Reset));
  Register #(.width(32), .trigger("falling")) register_10 (.D(DI), .en(Ld05), .Q(R05), .clk(Clk), .clr(Reset));
  Register #(.width(32), .trigger("falling")) register_11 (.D(DI), .en(Ld09), .Q(R09), .clk(Clk), .clr(Reset));
  Register #(.width(32), .trigger("falling")) register_12 (.D(DI), .en(Ld13), .Q(R13), .clk(Clk), .clr(Reset));
  Register #(.width(32), .trigger("falling")) register_13 (.D(DI), .en(Ld17), .Q(R17), .clk(Clk), .clr(Reset));
  Register #(.width(32), .trigger("falling")) register_14 (.D(DI), .en(Ld21), .Q(R21), .clk(Clk), .clr(Reset));
  Register #(.width(32), .trigger("falling")) register_15 (.D(DI), .en(Ld25), .Q(R25), .clk(Clk), .clr(Reset));
  Register #(.width(32), .trigger("falling")) Rlow (.D(Low), .en(Low_High), .Q(out_15), .clk(Clk), .clr(Reset));
  Register #(.width(32), .trigger("falling")) register_16 (.D(DI), .en(Ld02), .Q(R02), .clk(Clk), .clr(Reset));
  Register #(.width(32), .trigger("falling")) register_17 (.D(DI), .en(Ld06), .Q(R06), .clk(Clk), .clr(Reset));
  Register #(.width(32), .trigger("falling")) register_18 (.D(DI), .en(Ld10), .Q(R10), .clk(Clk), .clr(Reset));
  Register #(.width(32), .trigger("falling")) register_19 (.D(DI), .en(Ld14), .Q(R14), .clk(Clk), .clr(Reset));
  Register #(.width(32), .trigger("falling")) register_20 (.D(DI), .en(Ld18), .Q(R18), .clk(Clk), .clr(Reset));
  Register #(.width(32), .trigger("falling")) register_21 (.D(DI), .en(Ld22), .Q(R22), .clk(Clk), .clr(Reset));
  Register #(.width(32), .trigger("falling")) register_22 (.D(DI), .en(Ld26), .Q(R26), .clk(Clk), .clr(Reset));
  Register #(.width(32), .trigger("falling")) register_23 (.D(DI), .en(Ld30), .Q(R30), .clk(Clk), .clr(Reset));
  Register #(.width(32), .trigger("falling")) register_24 (.D(DI), .en(Ld03), .Q(R03), .clk(Clk), .clr(Reset));
  Register #(.width(32), .trigger("falling")) register_25 (.D(DI), .en(Ld07), .Q(R07), .clk(Clk), .clr(Reset));
  Register #(.width(32), .trigger("falling")) register_26 (.D(DI), .en(Ld11), .Q(R11), .clk(Clk), .clr(Reset));
  Register #(.width(32), .trigger("falling")) register_27 (.D(DI), .en(Ld15), .Q(R15), .clk(Clk), .clr(Reset));
  Register #(.width(32), .trigger("falling")) register_28 (.D(DI), .en(Ld19), .Q(R19), .clk(Clk), .clr(Reset));
  Register #(.width(32), .trigger("falling")) register_29 (.D(DI), .en(Ld23), .Q(R23), .clk(Clk), .clr(Reset));
  Register #(.width(32), .trigger("falling")) register_30 (.D(DI), .en(Ld27), .Q(R27), .clk(Clk), .clr(Reset));
  Register #(.width(32), .trigger("falling")) register_31 (.D(SP), .en(SPW), .Q(out_17), .clk(Clk), .clr(Reset));
  Multiplexer #(.select(5), .width(32), .enable("false")) multiplexer_1 (
    .in0({32{1'b0}}), .in1(R01), .in2(R02), .in3(R03), .in4(R04), .in5(R05), .in6(R06), .in7(R07), .in8(R08),
    .in9(R09), .in10(R10), .in11(R11), .in12(R12), .in13(R13), .in14(R14), .in15(R15), .in16(R16),
    .in17(R17), .in18(R18), .in19(R19), .in20(R20), .in21(R21), .in22(R22), .in23(R23), .in24(R24),
    .in25(R25), .in26(R26), .in27(R27), .in28(R28), .in29(R29), .in30(R30), .in31(out_17), .out(out_13),
    .sel(SA));
  Multiplexer #(.select(5), .width(32), .enable("false")) multiplexer_2 (
    .in0({32{1'b0}}), .in1(R01), .in2(R02), .in3(R03), .in4(R04), .in5(R05), .in6(R06), .in7(R07), .in8(R08),
    .in9(R09), .in10(R10), .in11(R11), .in12(R12), .in13(R13), .in14(R14), .in15(R15), .in16(R16),
    .in17(R17), .in18(R18), .in19(R19), .in20(R20), .in21(R21), .in22(R22), .in23(R23), .in24(R24),
    .in25(R25), .in26(R26), .in27(R27), .in28(R28), .in29(R29), .in30(R30), .in31(out_17), .out(out_14),
    .sel(SB));

  // Other names for the same wires on the sheet: A[31:0] = out_13; B[31:0] = out_14; IHi[31:0] = High;
  //   ILo[31:0] = Low; RHi[31:0] = out_16; RLow[31:0] = out_15; Rst = Reset; RW = Red_Write; SP_t[31:0] = out_17;
  //   SPIn[31:0] = SP; Whl = Low_High

  // Notes on the sheet:
  //   Selector A
  //   Selector B
  //   Inputs
  //   Data Address
  //   Data In
  //   SP R/W
  //   Registros
  //   High-Low
  //   Outputs
endmodule

module Instruction_Decoder_2 (
  input  [31:0] DI,
  input  RW,
  input  Clk,
  input  Rst,
  output [5:0] Op,
  output [5:0] Func__Code,
  output [25:0] Jmp,
  output [4:0] RS,
  output [4:0] RT,
  output [4:0] RD,
  output [31:0] Sign_Const,
  output [31:0] Unsgn_Const
);

  Register #(.width(32), .trigger("falling")) register_1 (
    .D(DI), .en(RW), .Q({Op, Jmp[25:6], Func__Code}), .clk(Clk), .clr(Rst));
  assign Sign_Const = {{16{Jmp[15]}}, {Jmp[15:6], Func__Code}};  // Bit_Extender bit_extender_1
  assign Unsgn_Const = {{16{1'b0}}, {Jmp[15:6], Func__Code}};  // Bit_Extender bit_extender_2

  assign Jmp[5:0] = Func__Code;
  assign RD = Jmp[15:11];
  assign RS = Jmp[25:21];
  assign RT = Jmp[20:16];

  // Other names for the same wires on the sheet: Destiny[25:0] = {Jmp[25:6], Func__Code}; FC[5:0] = Func__Code;
  //   K[15:0] = {Jmp[15:6], Func__Code}

  // Notes on the sheet:
  //   Inputs
  //   Outputs
endmodule

// BC
module Branch_Control (
  input  [1:0] in_1,
  input  [31:0] in_2,
  input  in_3,
  input  in_4,
  input  in_5,
  input  [31:0] in_6,
  input  [2:0] in_7,
  input  [25:0] in_8,
  input  [31:0] in_9,
  output [31:0] Next_PC
);

  wire Flag, Lez, Neq;
  wire [31:0] adder_1_out, adder_2_out, multiplexer_2_out, shifter_1_out;

  Multiplexer #(.select(3), .enable("false")) multiplexer_1 (
    .in0(in_3), .in1(Lez), .in2(Neq), .in6(in_5), .in7(in_4), .out(Flag), .sel(in_7));  // open: in3, in4, in5
  Adder #(.width(32)) adder_1 (.a(in_6), .b(32'h4), .out(adder_1_out));  // open: cin, cout
  Shifter #(.width(32)) shifter_1 (.in(in_9), .\dist (5'b00010), .out(shifter_1_out));
  not not_1 (Neq, in_3);
  Adder #(.width(32)) adder_2 (.a(adder_1_out), .b(shifter_1_out), .out(adder_2_out));  // open: cin, cout
  not not_2 (Lez, in_4);
  Multiplexer #(.width(32), .enable("false")) multiplexer_2 (
    .in0(adder_1_out), .in1(adder_2_out), .out(multiplexer_2_out), .sel(Flag));
  Multiplexer #(.select(2), .width(32), .enable("false")) multiplexer_3 (
    .in0(adder_1_out), .in1(multiplexer_2_out), .in2(in_2), .in3({in_6[31:28], in_8, 2'b00}), .out(Next_PC),
    .sel(in_1));

  // Other names for the same wires on the sheet: Destiny[25:0] = in_8; PC[31:0] = in_6; BcS[1:0] = in_1;
  //   FlagsS[2:0] = in_7; Ltz = in_5; Neg = in_5; Offset[31:0] = in_9; Gtz = in_4; Pos = in_4; Register[31:0] = in_2;
  //   Eq = in_3; Zero = in_3
endmodule

// DATAPATH
module DataPath (
  input  in_1,
  input  [31:0] DI,
  input  in_3,
  input  in_4,
  input  in_5,
  input  [1:0] in_6,
  input  in_7,
  input  [1:0] in_8,
  input  in_9,
  input  [1:0] in_10,
  input  in_11,
  input  in_12,
  input  [2:0] in_13,
  input  in_14,
  input  [2:0] in_15,
  input  in_16,
  input  [2:0] in_17,
  input  [6:0] kbd_data,
  input  avail,
  output [31:0] Address,
  output [31:0] Data_Out,
  output [5:0] Opcode,
  output [5:0] Funcode,
  output [6:0] out_24
);

  wire Neg, Pos, Zero;
  wire [4:0] DA, RD, RS, RT;
  wire [25:0] Destiny;
  wire [31:0] B, bit_extender_1_out, Branch_Control_next_pc, Hi, IHi, ILw, K, kbd, Lw, multiplexer_1_out,
       multiplexer_3_out, multiplexer_4_out, PC, R, rd_t, SP, UK;
  wire [31:7] A;

  Random #(.width(32)) random_1 (.clk(in_5), .out(rd_t));  // open: next, clr
  Multiplexer #(.select(3), .width(32), .enable("false")) multiplexer_1 (
    .in0(R), .in1(DI), .in3(Lw), .in5(Hi), .in6(rd_t), .in7(kbd), .out(multiplexer_1_out), .sel(in_13));  // open: in2, in4
  Multiplexer #(.width(5), .enable("false")) multiplexer_2 (.in0(RD), .in1(RT), .out(DA), .sel(in_1));
  Register_File_2 register_file_1 (
    .Red_Write(in_14), .DA(DA), .DI(multiplexer_1_out), .SA(RS), .Clk(in_5), .Reset(in_7), .SB(RT),
    .Low_High(in_12), .SP(R), .SP_RW(in_16), .Low(ILw), .High(IHi), .out_13({A, out_24}), .out_14(B),
    .out_15(Lw), .out_16(Hi), .out_17(SP));
  Instruction_Decoder_2 instruction_decoder_1 (
    .DI(DI), .Op(Opcode), .Func__Code(Funcode), .Jmp(Destiny), .RS(RS), .RT(RT), .RD(RD), .Sign_Const(K),
    .RW(in_9), .Clk(in_5), .Rst(in_7), .Unsgn_Const(UK));
  Branch_Control Branch_Control (
    .in_1(in_8), .in_2({A, out_24}), .in_3(Zero), .in_4(Pos), .in_5(Neg), .in_6(PC), .in_7(in_17),
    .in_8(Destiny), .Next_PC(Branch_Control_next_pc), .in_9(K));
  Register #(.width(32), .trigger("falling")) register_1 (
    .D(Branch_Control_next_pc), .en(in_11), .Q(PC), .clk(in_5), .clr(in_7));
  Multiplexer #(.width(32), .enable("false")) multiplexer_3 (
    .in0({A, out_24}), .in1(SP), .out(multiplexer_3_out), .sel(in_4));
  Multiplexer #(.select(2), .width(32), .enable("false")) multiplexer_4 (
    .in0(B), .in1(K), .in2(UK), .in3(32'h4), .out(multiplexer_4_out), .sel(in_6));
  Multiplexer #(.select(2), .width(32), .enable("false")) multiplexer_5 (
    .in0(PC), .in1(R), .in2(SP), .out(Address), .sel(in_10));  // open: in3
  Multiplexer #(.width(32), .enable("false")) multiplexer_6 (.in0(B), .in1({A, out_24}), .out(Data_Out), .sel(in_3));
  ALU_2 alu_1 (
    .in_1(multiplexer_3_out), .in_2(multiplexer_4_out), .S(in_15), .Lo(ILw), .R(R), .Hi(IHi), .Positive(Pos),
    .Zero(Zero), .Negative(Neg));
  assign bit_extender_1_out = {{25{1'b0}}, kbd_data};  // Bit_Extender bit_extender_1
  Multiplexer #(.width(32), .enable("false")) multiplexer_7 (
    .in0(bit_extender_1_out), .in1({32{1'b1}}), .out(kbd), .sel(avail));
  // Probe on PC
  // Probe on RS
  // Probe on RT
  // Probe on RD
  // Probe on DA
  // Probe on K
  // Probe on UK
  // Probe on Destiny
  // Probe on R
  // Probe on PC

  // Other names for the same wires on the sheet: A[6:0] = out_24; Addr[1:0] = in_10; ALUS[2:0] = in_15; AS = in_4;
  //   BcS[1:0] = in_8; BS[1:0] = in_6; Clk = in_5; DAS = in_1; DIS[2:0] = in_13; DOS = in_3; FC[5:0] = Funcode;
  //   FlagsS[2:0] = in_17; IM_RW = in_9; LH_RW = in_12; Op[5:0] = Opcode; PC_RW = in_11; Ram[31:0] = DI; Reset = in_7;
  //   RF_RW = in_14; SP_RW = in_16

  // Notes on the sheet:
  //   DEBUG
endmodule

module MemoryManager (
  input  [31:0] Addres_In,
  input  [31:0] Ram_out_0,
  input  [31:0] Ram_out_1,
  input  [31:0] Ram_out_2,
  input  [31:0] Ram_out_3,
  input  [3:0] Read_Time,
  input  Clk,
  input  Rst,
  input  [3:0] Write_Time,
  input  Start,
  input  R_W,
  output [31:0] From_RAM,
  output [3:0] Mask,
  output [15:0] ADDR,
  output [1:0] Bank,
  output RAMReady,
  output Chip_Select,
  output RAM_Write
);

  wire Clear, comparator_1_lt, demultiplexer_1_out0, IsFetch, or_2_out, Wait_q;
  wire [3:0] counter_1_q, Time;
  wire [31:0] multiplexer_2_out;

  Multiplexer #(.width(4), .enable("false")) multiplexer_1 (.in0(Read_Time), .in1(Write_Time), .out(Time), .sel(R_W));
  D_Flip_Flop Wait (.clk(Clk), .D(demultiplexer_1_out0), .Q(Wait_q));  // open: Qn, preset, en, reset
  or or_1 (Chip_Select, Wait_q, Start);
  Counter #(.width(4), .max('hf)) counter_1 (
    .count(Chip_Select), .Q(counter_1_q), .clk(Clk), .clr(or_2_out));  // open: load, D, carry
  or or_2 (or_2_out, Rst, Clear);
  Demultiplexer #(.enable("false")) demultiplexer_1 (
    .out0(demultiplexer_1_out0), .out1(RAMReady), .in(Chip_Select), .sel(IsFetch));
  Comparator #(.width(4), .mode("unsigned")) comparator_1 (
    .a(counter_1_q), .b(Time), .lt(comparator_1_lt));  // open: gt, eq
  not not_1 (IsFetch, comparator_1_lt);
  D_Flip_Flop End (.clk(Clk), .D(RAMReady), .Q(Clear));  // open: Qn, preset, en, reset
  Multiplexer #(.select(2), .width(32), .enable("false")) multiplexer_2 (
    .in0(Ram_out_0), .in1(Ram_out_1), .in2(Ram_out_2), .in3(Ram_out_3), .out(multiplexer_2_out),
    .sel(Addres_In[3:2]));
  Decoder #(.select(2), .enable("false")) decoder_1 (
    .out0(Mask[0]), .out1(Mask[1]), .out2(Mask[2]), .out3(Mask[3]), .sel(Addres_In[3:2]));
  Convert convert_1 (.Input(multiplexer_2_out), .Output(From_RAM));
  and and_1 (RAM_Write, R_W, Chip_Select);

  assign ADDR = Addres_In[19:4];
  assign Bank = Addres_In[3:2];

  // Other names for the same wires on the sheet: Block[15:0] = Addres_In[19:4]; End = RAMReady; Count = Chip_Select;
  //   CS = Chip_Select; RAM_Wr = Chip_Select; RW = R_W

  // Notes on the sheet:
  //   ADDRESS
  //   DATA FROM RAM
  //   RAM TIMING
  //   CONTROL SIGNALS
  //   TIMER
  //   FLOW CONTROL
endmodule

module Convert (
  input  [31:0] Input,
  output [31:0] Output
);


  assign Output = {Input[7:0], Input[15:8], Input[23:16], Input[31:24]};
endmodule

module Switch_Decoder (
  input  [5:0] OpCode,
  input  [5:0] FunCode,
  output addi,
  output beq,
  output slti,
  output add,
  output \and ,
  output nop,
  output andi,
  output bne,
  output sltiu,
  output sub,
  output \or ,
  output push,
  output ori,
  output blez,
  output lw,
  output pop,
  output mul,
  output \nor ,
  output xori,
  output bgtz,
  output sw,
  output tty,
  output mulu,
  output \xor ,
  output jump,
  output bltz,
  output div,
  output mfhi,
  output halt,
  output mflo,
  output divu,
  output rnd,
  output slt,
  output jr,
  output kbd,
  output sltu
);

  wire and_18_out, and_19_out, and_20_out, and_21_out, and_22_out, and_23_out, and_24_out, and_25_out,
       and_34_out, and_35_out, and_36_out, and_37_out, and_38_out, and_39_out, and_40_out, and_48_out,
       and_49_out, and_50_out, and_51_out, and_52_out, and_53_out, and_54_out, special, stack, Tipo_R;

  and and_1 (addi, ~OpCode[0], ~OpCode[1], ~OpCode[2], OpCode[3], ~OpCode[4], ~OpCode[5]);  // AND_Gate
  and and_2 (andi, ~OpCode[0], ~OpCode[1], OpCode[2], OpCode[3], ~OpCode[4], ~OpCode[5]);  // AND_Gate
  and and_3 (ori, OpCode[0], ~OpCode[1], OpCode[2], OpCode[3], ~OpCode[4], ~OpCode[5]);  // AND_Gate
  and and_4 (xori, ~OpCode[0], OpCode[1], OpCode[2], OpCode[3], ~OpCode[4], ~OpCode[5]);  // AND_Gate
  and and_5 (jump, ~OpCode[0], OpCode[1], ~OpCode[2], ~OpCode[3], ~OpCode[4], ~OpCode[5]);  // AND_Gate
  and and_6 (Tipo_R, ~OpCode[0], ~OpCode[1], ~OpCode[2], ~OpCode[3], ~OpCode[4], ~OpCode[5]);  // AND_Gate
  and and_7 (beq, ~OpCode[0], ~OpCode[1], OpCode[2], ~OpCode[3], ~OpCode[4], ~OpCode[5]);  // AND_Gate
  and and_8 (bne, OpCode[0], ~OpCode[1], OpCode[2], ~OpCode[3], ~OpCode[4], ~OpCode[5]);  // AND_Gate
  and and_9 (blez, ~OpCode[0], OpCode[1], OpCode[2], ~OpCode[3], ~OpCode[4], ~OpCode[5]);  // AND_Gate
  and and_10 (bgtz, OpCode[0], OpCode[1], OpCode[2], ~OpCode[3], ~OpCode[4], ~OpCode[5]);  // AND_Gate
  and and_11 (bltz, OpCode[0], ~OpCode[1], ~OpCode[2], ~OpCode[3], ~OpCode[4], ~OpCode[5]);  // AND_Gate
  and and_12 (stack, ~OpCode[0], ~OpCode[1], ~OpCode[2], OpCode[3], OpCode[4], OpCode[5]);  // AND_Gate
  and and_13 (slti, ~OpCode[0], OpCode[1], ~OpCode[2], OpCode[3], ~OpCode[4], ~OpCode[5]);  // AND_Gate
  and and_14 (lw, OpCode[0], OpCode[1], ~OpCode[2], ~OpCode[3], ~OpCode[4], OpCode[5]);  // AND_Gate
  and and_15 (sw, OpCode[0], OpCode[1], ~OpCode[2], OpCode[3], ~OpCode[4], OpCode[5]);  // AND_Gate
  and and_16 (special, OpCode[0], OpCode[1], OpCode[2], OpCode[3], OpCode[4], OpCode[5]);
  and and_17 (sltiu, OpCode[0], OpCode[1], ~OpCode[2], OpCode[3], ~OpCode[4], ~OpCode[5]);  // AND_Gate
  and and_18 (and_18_out, ~FunCode[0], ~FunCode[1], ~FunCode[2], ~FunCode[3], ~FunCode[4], FunCode[5]);  // AND_Gate
  and and_19 (and_19_out, ~FunCode[0], FunCode[1], ~FunCode[2], ~FunCode[3], ~FunCode[4], FunCode[5]);  // AND_Gate
  and and_20 (and_20_out, ~FunCode[0], ~FunCode[1], ~FunCode[2], FunCode[3], FunCode[4], ~FunCode[5]);  // AND_Gate
  and and_21 (and_21_out, FunCode[0], ~FunCode[1], ~FunCode[2], FunCode[3], FunCode[4], ~FunCode[5]);  // AND_Gate
  and and_22 (and_22_out, ~FunCode[0], FunCode[1], ~FunCode[2], FunCode[3], FunCode[4], ~FunCode[5]);  // AND_Gate
  and and_23 (and_23_out, FunCode[0], FunCode[1], ~FunCode[2], FunCode[3], FunCode[4], ~FunCode[5]);  // AND_Gate
  and and_24 (and_24_out, ~FunCode[0], FunCode[1], ~FunCode[2], FunCode[3], ~FunCode[4], FunCode[5]);  // AND_Gate
  and and_25 (and_25_out, FunCode[0], FunCode[1], ~FunCode[2], FunCode[3], ~FunCode[4], FunCode[5]);  // AND_Gate
  and and_26 (add, and_18_out, Tipo_R);
  and and_27 (sub, and_19_out, Tipo_R);
  and and_28 (mul, and_20_out, Tipo_R);
  and and_29 (mulu, and_21_out, Tipo_R);
  and and_30 (div, and_22_out, Tipo_R);
  and and_31 (divu, and_23_out, Tipo_R);
  and and_32 (slt, and_24_out, Tipo_R);
  and and_33 (sltu, and_25_out, Tipo_R);
  and and_34 (and_34_out, ~FunCode[0], ~FunCode[1], FunCode[2], ~FunCode[3], ~FunCode[4], FunCode[5]);  // AND_Gate
  and and_35 (and_35_out, FunCode[0], ~FunCode[1], FunCode[2], ~FunCode[3], ~FunCode[4], FunCode[5]);  // AND_Gate
  and and_36 (and_36_out, FunCode[0], FunCode[1], FunCode[2], ~FunCode[3], ~FunCode[4], FunCode[5]);  // AND_Gate
  and and_37 (and_37_out, ~FunCode[0], ~FunCode[1], ~FunCode[2], FunCode[3], ~FunCode[4], FunCode[5]);  // AND_Gate
  and and_38 (and_38_out, ~FunCode[0], ~FunCode[1], ~FunCode[2], ~FunCode[3], FunCode[4], ~FunCode[5]);  // AND_Gate
  and and_39 (and_39_out, ~FunCode[0], FunCode[1], ~FunCode[2], ~FunCode[3], FunCode[4], ~FunCode[5]);  // AND_Gate
  and and_40 (and_40_out, ~FunCode[0], ~FunCode[1], ~FunCode[2], FunCode[3], ~FunCode[4], ~FunCode[5]);  // AND_Gate
  and and_41 (\and , and_34_out, Tipo_R);
  and and_42 (\or , and_35_out, Tipo_R);
  and and_43 (\nor , and_36_out, Tipo_R);
  and and_44 (\xor , and_37_out, Tipo_R);
  and and_45 (mfhi, and_38_out, Tipo_R);
  and and_46 (mflo, and_39_out, Tipo_R);
  and and_47 (jr, and_40_out, Tipo_R);
  and and_48 (and_48_out, ~FunCode[0], ~FunCode[1], ~FunCode[2], ~FunCode[3], ~FunCode[4], ~FunCode[5]);  // AND_Gate
  and and_49 (and_49_out, FunCode[0], ~FunCode[1], ~FunCode[2], ~FunCode[3], ~FunCode[4], ~FunCode[5]);  // AND_Gate
  and and_50 (and_50_out, ~FunCode[0], ~FunCode[1], ~FunCode[2], ~FunCode[3], ~FunCode[4], ~FunCode[5]);  // AND_Gate
  and and_51 (and_51_out, FunCode[0], ~FunCode[1], ~FunCode[2], ~FunCode[3], ~FunCode[4], ~FunCode[5]);  // AND_Gate
  and and_52 (and_52_out, FunCode[0], FunCode[1], FunCode[2], FunCode[3], FunCode[4], FunCode[5]);
  and and_53 (and_53_out, ~FunCode[0], FunCode[1], ~FunCode[2], ~FunCode[3], ~FunCode[4], ~FunCode[5]);  // AND_Gate
  and and_54 (and_54_out, ~FunCode[0], ~FunCode[1], FunCode[2], ~FunCode[3], ~FunCode[4], ~FunCode[5]);  // AND_Gate
  and and_55 (nop, and_48_out, Tipo_R);
  and and_56 (push, and_49_out, stack);
  and and_57 (pop, and_50_out, stack);
  and and_58 (tty, and_51_out, special);
  and and_59 (halt, and_52_out, special);
  and and_60 (rnd, and_53_out, special);
  and and_61 (kbd, and_54_out, special);

  // Other names for the same wires on the sheet: f0 = FunCode[0]; f1 = FunCode[1]; f2 = FunCode[2]; f3 = FunCode[3];
  //   f4 = FunCode[4]; f5 = FunCode[5]; o0 = OpCode[0]; o1 = OpCode[1]; o2 = OpCode[2]; o3 = OpCode[3];
  //   o4 = OpCode[4]; o5 = OpCode[5]

  // Notes on the sheet:
  //   OP CODE
  //   GROUP
  //   FUNC CODE
endmodule

module Type_Arithmetic (
  input  in_1,
  input  in_2,
  input  in_3,
  input  in_4,
  input  in_5,
  input  in_6,
  input  in_7,
  input  in_8,
  input  in_9,
  input  in_10,
  input  in_11,
  input  in_12,
  input  in_13,
  input  in_14,
  input  in_15,
  input  in_16,
  input  in_17,
  output out_18,
  output out_19,
  output [2:0] out_20,
  output out_21,
  output [2:0] out_22,
  output [1:0] out_23
);

  wire not_1_out, or_5_out, or_6_out, or_7_out, or_8_out;
  wire [1:0] or_1_out;
  wire [2:0] or_2_out;

  not not_1 (not_1_out, in_14);
  or or_1 (or_1_out[0], in_15, in_14);
  or or_2 (or_2_out[0], in_6, in_3, in_5, in_11, in_9, in_13);
  or or_3 (or_2_out[1], in_13, in_4, in_5, in_8, in_9, in_12);
  or or_4 (or_2_out[2], in_7, in_8, in_6, in_9);
  or or_5 (or_5_out, in_10, in_11, in_12, in_13);
  and and_1 (out_21, or_5_out, in_1);
  and and_2 (or_1_out[1], in_15, not_1_out);
  assign out_23 = {in_16, 1'b0} & {2{in_1}};  // AND_Gate and_3, 2 bits wide
  or or_6 (or_6_out, or_2_out[0], or_2_out[1], or_2_out[2]);
  or or_7 (or_7_out, in_2, or_6_out);
  assign out_20 = or_2_out & {3{in_1}};  // AND_Gate and_4, 3 bits wide
  assign out_22 = {in_14, or_1_out} & {3{in_1}};  // AND_Gate and_5, 3 bits wide
  or or_8 (or_8_out, or_7_out, in_14, in_15);
  and and_6 (out_19, or_8_out, ~in_11, ~in_12, ~in_13, in_1);  // AND_Gate

  assign out_18 = in_1;

  // Other names for the same wires on the sheet: jr = in_16; mfhi = in_14; EN = in_1; PC = in_1; add = in_2;
  //   and = in_4; div = in_12; divu = in_13; LH = out_21; mflo = in_15; mul = in_10; mulu = in_11; nop = in_17;
  //   nor = in_7; or = in_5; Rf_Rw = out_19; S_ALU[2:0] = out_20; S_BC[1:0] = out_23; S_Di[2:0] = out_22; slt = in_8;
  //   sltu = in_9; sub = in_3; xor = in_6
endmodule

module Type_Inmediate (
  input  in_1,
  input  in_2,
  input  in_3,
  input  in_4,
  input  in_5,
  input  in_6,
  input  in_7,
  output [2:0] out_8,
  output [1:0] out_9,
  output out_10,
  output out_11,
  output out_12
);

  wire or_2_out, or_3_out;
  wire [0:0] or_1_out;
  wire [2:0] or_5_out;

  or or_1 (or_1_out[0], in_2, in_3, in_4, in_5, in_6, in_7);
  and and_1 (out_10, or_1_out[0], in_1);
  assign out_9 = {1'b0, or_1_out[0]} & {2{in_1}};  // AND_Gate and_2, 2 bits wide
  or or_2 (or_2_out, in_4, in_7);
  or or_3 (or_3_out, in_6, in_3);
  or or_4 (or_5_out[2], in_7, in_6, in_5);
  or or_5 (or_5_out[0], in_5, or_2_out);
  or or_6 (or_5_out[1], or_2_out, or_3_out);
  assign out_8 = or_5_out & {3{in_1}};  // AND_Gate and_3, 3 bits wide

  assign out_11 = in_1;
  assign out_12 = in_1;

  // Other names for the same wires on the sheet: En = in_1; PC = in_1; RW_RF = in_1; addi = in_2; andi = in_3;
  //   ori = in_4; S_ALU[2:0] = out_8; S_B[1:0] = out_9; S_DA = out_10; slti = in_6; sltiu = in_7; xori = in_5
endmodule

module Type_Branch (
  input  in_1,
  input  in_2,
  input  in_3,
  input  in_4,
  input  in_5,
  input  in_6,
  input  in_7,
  output out_8,
  output [2:0] out_9,
  output [1:0] out_10,
  output [2:0] out_11
);

  wire Or_R;
  wire [0:0] or_4_out;
  wire [2:0] or_3_out;

  or or_1 (Or_R, in_2, in_3, in_4, in_5, in_6);
  or or_2 (or_3_out[2], in_4, in_6);
  nor nor_1 (or_3_out[1], in_2, in_5);
  or or_3 (or_3_out[0], in_5, in_4);
  or or_4 (or_4_out[0], Or_R, in_7);
  assign out_11 = or_3_out & {3{in_1}};  // AND_Gate and_1, 3 bits wide
  assign out_9 = {2'b00, Or_R} & {3{in_1}};  // AND_Gate and_2, 3 bits wide
  assign out_10 = {in_7, or_4_out[0]} & {2{in_1}};  // AND_Gate and_3, 2 bits wide

  assign out_8 = in_1;

  // Other names for the same wires on the sheet: Jump = in_7; EN = in_1; PC = in_1; ALUS[2:0] = out_9;
  //   BcS[1:0] = out_10; Eq = in_2; FlagsS[2:0] = out_11; Gtz = in_4; Lez = in_5; Ltz = in_6; Neq = in_3
endmodule

module Type_Word (
  input  in_1,
  input  in_2,
  input  in_3,
  input  in_4,
  input  in_5,
  output out_6,
  output out_7,
  output out_8,
  output [2:0] out_9,
  output [1:0] out_10,
  output out_11,
  output [1:0] out_12,
  output out_13,
  output out_14
);

  wire AdrlS, d_ff_1_q, d_ff_2_q, Endlw, Endsw, PCs, StartRaml, StartRams, ToClk, toClk_t;

  or or_1 (out_11, Endlw, Endsw);
  or or_2 (out_13, StartRaml, StartRams);
  D_Flip_Flop d_ff_1 (.clk(in_2), .D(ToClk), .Q(d_ff_1_q));  // open: Qn, preset, en, reset
  D_Flip_Flop d_ff_2 (.clk(in_2), .D(toClk_t), .Q(d_ff_2_q));  // open: Qn, preset, en, reset
  and and_1 (StartRaml, in_1, in_3);
  and and_2 (StartRams, in_1, in_5);
  or or_3 (AdrlS, StartRaml, d_ff_1_q);
  or or_4 (out_14, out_6, PCs);
  or or_5 (out_8, StartRams, d_ff_2_q);
  Demultiplexer #(.enable("false")) demultiplexer_1 (.out0(ToClk), .out1(out_6), .in(AdrlS), .sel(in_4));
  Demultiplexer #(.enable("false")) demultiplexer_2 (.out0(toClk_t), .out1(PCs), .in(out_8), .sel(in_4));
  or or_6 (out_10[0], AdrlS, out_8);
  or or_7 (out_12[0], AdrlS, out_8);
  D_Flip_Flop d_ff_3 (.clk(in_2), .D(PCs), .Q(Endsw));  // open: Qn, preset, en, reset
  D_Flip_Flop d_ff_4 (.clk(in_2), .D(out_6), .Q(Endlw));  // open: Qn, preset, en, reset

  assign out_7 = out_6;
  assign out_9 = {2'b00, out_6};
  assign out_10[1] = 1'b0;
  assign out_12[1] = 1'b0;

  // Other names for the same wires on the sheet: AdrS[0] = out_12[0]; BlS = AdrlS; BS[0] = out_10[0]; Clk = in_2;
  //   DAwS = out_6; DIS[0] = out_6; DIwS = out_6; PCl = out_6; Rf_w = out_6; EN = in_1; ENDw = out_11;
  //   LoadWord = in_3; PC = out_14; RamReady = in_4; AdrsS = out_8; BsS = out_8; RamW = out_8; StartRam = out_13;
  //   StoreWord = in_5

  // Notes on the sheet:
  //   LOAD
  //   STORE
  //   OUTS
endmodule

module Type_Specials (
  input  in_1,
  input  in_2,
  input  in_3,
  input  in_4,
  output out_5,
  output [2:0] out_6,
  output out_7,
  output out_8,
  output out_9
);

  wire [2:2] or_1_out;

  and and_1 (out_7, in_4, in_1);
  or or_1 (or_1_out[2], in_2, in_3);
  and and_2 (out_5, or_1_out[2], in_1);
  assign out_6 = {{2{or_1_out[2]}}, in_2} & {3{in_1}};  // AND_Gate and_3, 3 bits wide
  and and_4 (out_9, in_2, in_1);

  assign out_8 = in_1;

  // Other names for the same wires on the sheet: kbd = in_2; EN = in_1; PC = in_1; DiS[2:0] = out_6;
  //   kbd__Enable = out_9; Rf = out_5; rnd = in_3; tty = in_4; tty_Enable = out_7
endmodule

module Type_Stack (
  input  in_1,
  input  in_2,
  input  in_3,
  input  in_4,
  input  in_5,
  output out_6,
  output out_7,
  output out_8,
  output out_9,
  output [1:0] out_10,
  output out_11,
  output out_12,
  output [1:0] out_13,
  output out_14,
  output [2:0] out_15,
  output [2:0] out_16,
  output out_17
);

  wire AdrPopS, d_ff_1_q, d_ff_3_q, EndPop, EndPush, PCPush, StartRamPop, StartRamPush, ToClk, toClk_t;

  and and_1 (out_16[0], in_3, in_2);
  or or_1 (out_9, out_6, out_16[0]);
  or or_2 (out_13[1], out_6, out_16[0]);
  and and_2 (StartRamPop, in_3, in_1);
  D_Flip_Flop d_ff_1 (.clk(in_5), .D(ToClk), .Q(d_ff_1_q));  // open: Qn, preset, en, reset
  or or_3 (AdrPopS, StartRamPop, d_ff_1_q);
  or or_4 (out_10[1], AdrPopS, out_7);
  or or_5 (out_14, out_6, out_16[0]);
  Demultiplexer #(.enable("false")) demultiplexer_1 (.out0(ToClk), .out1(out_6), .in(AdrPopS), .sel(in_4));
  D_Flip_Flop d_ff_2 (.clk(in_5), .D(out_16[0]), .Q(StartRamPush));  // open: Qn, preset, en, reset
  D_Flip_Flop d_ff_3 (.clk(in_5), .D(toClk_t), .Q(d_ff_3_q));  // open: Qn, preset, en, reset
  or or_6 (out_7, StartRamPush, d_ff_3_q);
  or or_7 (out_17, EndPop, EndPush);
  or or_8 (out_11, out_6, PCPush);
  Demultiplexer #(.enable("false")) demultiplexer_2 (.out0(toClk_t), .out1(PCPush), .in(out_7), .sel(in_4));
  or or_9 (out_12, StartRamPop, StartRamPush);
  D_Flip_Flop d_ff_4 (.clk(in_5), .D(out_6), .Q(EndPop));  // open: Qn, preset, en, reset
  D_Flip_Flop d_ff_5 (.clk(in_5), .D(PCPush), .Q(EndPush));  // open: Qn, preset, en, reset

  assign out_8 = out_7;
  assign out_10[0] = 1'b0;
  assign out_13[0] = out_13[1];
  assign out_15 = {2'b00, out_6};
  assign out_16[2:1] = 2'b00;

  // Other names for the same wires on the sheet: AdrS[1] = out_10[1]; ALU0S = out_16[0]; ALUS[0] = out_16[0];
  //   APushS = out_16[0]; BPushS = out_16[0]; SP_RW_Push = out_16[0]; AS = out_9; BS[1:0] = {2{out_13[1]}};
  //   Clk = in_5; APopS = out_6; BPopS = out_6; Di_S = out_6; DiS[0] = out_6; PCPop = out_6; Rf_Rw = out_6;
  //   SP_RW_Pop = out_6; EN = in_3; EndStack = out_17; PC = out_11; Pop = in_1; Push = in_2; RamReady = in_4;
  //   AdrPushS = out_7; DoS = out_7; RamW = out_7; SP_RW = out_14; StartRam = out_12

  // Notes on the sheet:
  //   POP
  //   PUSH
  //   OUTS
endmodule

module Control_Unit_2 (
  input  [5:0] in_1,
  input  [5:0] in_2,
  input  in_3,
  input  in_4,
  input  in_5,
  output Output,
  output [2:0] out_7,
  output [2:0] out_8,
  output out_9,
  output out_10,
  output [1:0] out_11,
  output out_12,
  output out_13,
  output out_14,
  output [1:0] out_15,
  output out_16,
  output out_17,
  output [2:0] out_18,
  output out_19,
  output [1:0] out_20,
  output out_21,
  output out_22,
  output out_23,
  output out_24
);

  wire add, addi, \and , andi, beq, bgtz, blez, bltz, bne, d_ff_1_q, demultiplexer_1_out0,
       demultiplexer_1_out1, demultiplexer_2_out0, div, divu, EnableAl, EnableBranch, EnableInm,
       EnableSpecial, EnableStack, EnableWord, EndSt, Endw, halt_t, IDLE_q, jr, jump, kbd, LD_Ir_q, lw, mfhi,
       mflo, mul, mulu, Next, nop, \nor , not_1_out, \or , or_2_out, or_3_out, or_4_out, ori, PC_A, PC_B,
       PC_in, PC_Sp, PC_st, PC_W, pop, push, RamWst, RAMWw, RF_A, RF_in, RF_Sp, RF_st, RF_W, rnd, S_DaW,
       S_Din, slt, slti, sltiu, sltu, StarRamw, StartRamF, StartRamst, sub, sw, tty_t, TypeAl, TypeBranch,
       TypeInm, TypeSpecial, TypeWord, \xor , xori;
  wire [1:0] BC_S, S_AndrSt, S_AndrW, S_Bin, S_Bst, S_Bw, Sbc_A;
  wire [2:0] S_aluB, S_ALUin, S_ALUst, S_diA, S_DIsp, S_Dist, S_diW, Salu_A;

  Switch_Decoder switch_decoder_1 (
    .OpCode(in_1), .FunCode(in_2), .beq(beq), .slti(slti), .add(add), .\and (\and ), .nop(nop), .andi(andi),
    .bne(bne), .sltiu(sltiu), .sub(sub), .\or (\or ), .push(push), .ori(ori), .blez(blez), .lw(lw),
    .pop(pop), .mul(mul), .\nor (\nor ), .xori(xori), .bgtz(bgtz), .sw(sw), .tty(tty_t), .mulu(mulu),
    .\xor (\xor ), .jump(jump), .bltz(bltz), .div(div), .mfhi(mfhi), .halt(halt_t), .mflo(mflo), .divu(divu),
    .rnd(rnd), .slt(slt), .jr(jr), .kbd(kbd), .sltu(sltu), .addi(addi));
  Demultiplexer #(.enable("false")) demultiplexer_1 (
    .out0(demultiplexer_1_out0), .out1(demultiplexer_1_out1), .in(IDLE_q), .sel(not_1_out));
  D_Flip_Flop IDLE (.clk(in_3), .D(demultiplexer_1_out0), .Q(IDLE_q), .preset(in_4));  // open: Qn, en, reset
  not not_1 (not_1_out, in_4);
  or or_1 (StartRamF, Next, demultiplexer_1_out1);
  D_Flip_Flop d_ff_1 (.clk(in_3), .D(demultiplexer_2_out0), .Q(d_ff_1_q));  // open: Qn, preset, en, reset
  Type_Arithmetic type_arithmetic_1 (
    .in_1(EnableAl), .in_2(add), .in_3(sub), .in_4(\and ), .in_5(\or ), .in_6(\xor ), .in_7(\nor ),
    .in_8(slt), .in_9(sltu), .in_10(mul), .in_11(mulu), .in_12(div), .in_13(divu), .in_14(mfhi),
    .in_15(mflo), .in_16(jr), .in_17(nop), .out_19(RF_A), .out_20(Salu_A), .out_23(Sbc_A), .out_21(out_9),
    .out_22(S_diA), .out_18(PC_A));
  Type_Inmediate type_inmediate_1 (
    .in_1(EnableInm), .in_2(addi), .in_3(andi), .in_4(ori), .in_5(xori), .in_6(slti), .in_7(sltiu),
    .out_10(S_Din), .out_11(PC_in), .out_12(RF_in), .out_9(S_Bin), .out_8(S_ALUin));
  or or_2 (or_2_out, StartRamF, d_ff_1_q);
  Demultiplexer #(.enable("false")) demultiplexer_2 (
    .out0(demultiplexer_2_out0), .out1(Output), .in(or_2_out), .sel(in_5));
  D_Flip_Flop LD_Ir (.clk(in_3), .D(Output), .Q(LD_Ir_q));  // open: Qn, preset, en, reset
  or or_3 (or_3_out, push, pop);
  Type_Branch type_branch_1 (
    .in_1(EnableBranch), .in_2(beq), .in_3(bne), .in_4(bgtz), .in_5(blez), .in_6(bltz), .in_7(jump),
    .out_8(PC_B), .out_9(S_aluB), .out_11(out_18), .out_10(BC_S));
  Type_Specials type_specials_1 (
    .in_1(EnableSpecial), .in_2(kbd), .in_3(rnd), .in_4(tty_t), .out_7(out_14), .out_8(PC_Sp), .out_5(RF_Sp),
    .out_6(S_DIsp), .out_9(out_22));
  or or_4 (or_4_out, halt_t, out_24);
  and and_1 (EnableStack, or_3_out, LD_Ir_q);
  and and_2 (EnableWord, TypeWord, LD_Ir_q);
  and and_3 (EnableSpecial, TypeSpecial, LD_Ir_q);
  and and_4 (EnableBranch, TypeBranch, LD_Ir_q);
  and and_5 (EnableInm, TypeInm, LD_Ir_q);
  and and_6 (EnableAl, TypeAl, LD_Ir_q);
  D_Flip_Flop #(.trigger("high")) Halt (.clk(in_3), .D(or_4_out), .Q(out_24));  // open: Qn, preset, en, reset
  or or_5 (Next, EndSt, Endw, EnableSpecial, EnableBranch, EnableInm, EnableAl);
  Type_Word type_word_1 (
    .in_1(EnableWord), .in_2(in_3), .in_3(lw), .in_4(in_5), .in_5(sw), .out_11(Endw), .out_13(StarRamw),
    .out_9(S_diW), .out_14(PC_W), .out_10(S_Bw), .out_12(S_AndrW), .out_6(RF_W), .out_7(S_DaW), .out_8(RAMWw));
  Type_Stack type_stack_1 (
    .in_1(pop), .in_2(push), .in_3(EnableStack), .in_4(in_5), .in_5(in_3), .out_9(out_13), .out_14(out_23),
    .out_10(S_AndrSt), .out_17(EndSt), .out_16(S_ALUst), .out_11(PC_st), .out_15(S_Dist),
    .out_12(StartRamst), .out_6(RF_st), .out_7(RamWst), .out_8(out_16), .out_13(S_Bst));
  or or_6 (TypeBranch, beq, bne, blez, bgtz, bltz, jump);
  or or_7 (TypeInm, addi, andi, ori, xori, slti, sltiu);
  or or_8 (TypeAl, add, sub, \and , \or , \xor , \nor , slt, sltu, mul, mulu, div, divu, mfhi, mflo, jr, nop);
  assign out_7 = Salu_A | S_ALUin | S_aluB | S_ALUst;  // OR_Gate or_9, 3 bits wide
  assign out_15 = S_Bst | S_Bin | S_Bw;  // OR_Gate or_10, 2 bits wide
  assign out_20 = Sbc_A | BC_S;  // OR_Gate or_11, 2 bits wide
  or or_12 (TypeWord, lw, sw);
  or or_13 (TypeSpecial, kbd, rnd, tty_t);
  assign out_8 = S_diA | S_Dist | S_diW | S_DIsp;  // OR_Gate or_14, 3 bits wide
  assign out_11 = S_AndrSt | S_AndrW;  // OR_Gate or_15, 2 bits wide
  or or_16 (out_21, S_Din, S_DaW);
  or or_17 (out_12, RamWst, RAMWw);
  or or_18 (out_19, StarRamw, StartRamF, StartRamst);
  or or_19 (out_10, RF_A, RF_W, RF_st, RF_in, RF_Sp);
  or or_20 (out_17, PC_B, PC_Sp, PC_W, PC_st, PC_A, PC_in);

  // Other names for the same wires on the sheet: Clk = in_3; FuncCode[5:0] = in_2; HALT = out_24; En_KBD = out_22;
  //   kbd_En = out_22; L_LoHi = out_9; LH = out_9; LdIr = Output; OpCode[5:0] = in_1; PC = out_17; RamReady = in_5;
  //   RamW = out_12; Rf_Rw = out_10; S_Adr[1:0] = out_11; S_ALU[2:0] = out_7; S_A = out_13; S_Ast = out_13;
  //   S_B[1:0] = out_15; S_BC[1:0] = out_20; S_DA = out_21; S_Di[2:0] = out_8; S_DO = out_16; Flags_S[2:0] = out_18;
  //   S_flag[2:0] = out_18; SP = out_23; SPst = out_23; Start = in_4; StartRam = out_19; TTY = out_14;
  //   tty_En = out_14

  // Notes on the sheet:
  //   INPUTS
  //   SELECTORES
  //   LOADS
endmodule

module contador (
  input  in_1,
  input  in_2,
  input  in_3,
  input  in_4,
  input  [6:0] in_5,
  output halt,
  output [6:0] out_7,
  output Output
);

  wire and_1_out, comparator_1_eq, comparator_2_eq;
  wire [1:0] counter_2_q;
  wire [15:0] counter_1_q;

  // Probe on 16'hfff
  Counter #(.width(16), .max('hffff)) counter_1 (
    .count(1'b1), .Q(counter_1_q), .clk(in_1), .clr(in_2));  // open: load, D, carry
  Comparator #(.width(16)) comparator_1 (.a(16'hfff), .b(counter_1_q), .eq(comparator_1_eq));  // open: gt, lt
  // Probe on counter_1_q
  Counter #(.width(2), .max('h3)) counter_2 (
    .count(comparator_1_eq), .Q(counter_2_q), .clk(in_1));  // open: load, D, carry, clr
  Comparator #(.width(2)) comparator_2 (.a(counter_2_q), .b(2'b01), .eq(comparator_2_eq));  // open: gt, lt
  and and_1 (and_1_out, comparator_1_eq, ~comparator_2_eq);  // AND_Gate
  or or_1 (Output, in_4, and_1_out);
  Multiplexer #(.width(7)) multiplexer_1 (.in0(in_5), .in1(7'b1000000), .out(out_7), .sel(and_1_out));  // open: en
  or or_2 (halt, in_3, comparator_2_eq);

  // Other names for the same wires on the sheet: CLK = in_1; HLT = in_3; RST = in_2; TTY_DATA[6:0] = out_7;
  //   TTY_DATA_1[6:0] = in_5; TTY_EN = Output; TTY_EN_1 = in_4
endmodule
